# Fritzing sketch Carlson (saved by Fritzing 0.9.3b)
breadboards: 1

parts:
  MPU6050 = Header 8 [part_number=MPU6050 package=1x08_smd]
  Part2 = Breakout Board for Electret Microphone
  Part3 = MicroSD Card Module
  Part1 = Arduino Micro (Rev3)

nets:
  VCC: MPU6050.1, Part2.VCC, Part1.3V3
  GND: MPU6050.2, Part2.GND, Part3.GND, Part1.GND
  N1: MPU6050.3, Part1.D3/SCL
  N2: MPU6050.4, Part1.D2/SDA
  N3: MPU6050.8, Part1.D7
  N4: Part2.AUD, Part1.A0
  VCC_2: Part3.VCC, Part1.5V
  N5: Part3.MISO, Part1.MISO
  N6: Part3.MOSI, Part1.MOSI
  N7: Part3.SCK, Part1.SCK
  N8: Part3.CS, Part1.D10_PWM/A10

notes:
  MPU6050
  pins, from left to right:
  1-VCC
  2-GND
  3-SCL
  4-SDA
  5-XDA
  6-XCL
  7-ADO
  8-INT
  on Arduino Pro Micro, MISO is dig14, and MOSI is dig16, SCK is dig15
